// Logisim project control-logic.circ as structural Verilog: 1 circuit, main circuit control_logic
module control_logic (
  input  [31:0] Instruction,
  input  BrEq,
  input  BrLt,
  output PCSel,
  output RegWEn,
  output [2:0] ImmSel,
  output BrUn,
  output ASel,
  output BSel,
  output [3:0] ALUSel,
  output MemWEn,
  output [1:0] WBSel
);

  wire comparator_8_eq, comparator_9_eq, comparator_10_eq, comparator_11_eq, comparator_12_eq,
       comparator_13_eq, comparator_14_eq, comparator_15_eq, comparator_16_eq, comparator_17_eq,
       comparator_18_eq, comparator_19_eq, comparator_20_eq, comparator_21_eq, comparator_22_eq,
       comparator_23_eq, comparator_24_eq, comparator_25_eq, comparator_26_eq, comparator_27_eq, IS_ADD,
       IS_ADD_MUL_SUB, IS_ADDI, IS_AND, IS_ANDI, IS_ARITH, IS_I, IS_LOGICAL, IS_MUL, IS_MULH, IS_MULHU,
       IS_OR, IS_ORI, IS_R, IS_SLL, IS_SLL_MULH, IS_SLLI, IS_SLT, IS_SLTI, IS_SRA, IS_SRA_SRL, IS_SRAI,
       IS_SRL, IS_SRLI, IS_SUB, IS_XOR, IS_XORI;
  wire [5:0] ROM_INPUT;
  wire [15:14] rom_1_data;

  Comparator #(.width(7)) comparator_1 (.a(Instruction[6:0]), .b(7'b0010011), .eq(IS_I));  // open: gt, lt
  Comparator #(.width(7)) comparator_2 (.a(Instruction[6:0]), .b(7'b0110011), .eq(IS_R));  // open: gt, lt
  Comparator #(.width(7)) comparator_3 (.a(Instruction[31:25]), .b({7{1'b0}}), .eq(IS_LOGICAL));  // open: gt, lt
  Comparator #(.width(7)) comparator_4 (.a(Instruction[31:25]), .b(7'b0100000), .eq(IS_ARITH));  // open: gt, lt
  Comparator #(.width(3)) comparator_5 (.a(Instruction[14:12]), .b(3'b000), .eq(IS_ADD_MUL_SUB));  // open: gt, lt
  Comparator #(.width(3)) comparator_6 (.a(Instruction[14:12]), .b(3'b001), .eq(IS_SLL_MULH));  // open: gt, lt
  Comparator #(.width(3)) comparator_7 (.a(Instruction[14:12]), .b(3'b101), .eq(IS_SRA_SRL));  // open: gt, lt
  ROM #(.addrWidth(6), .dataWidth(16)) rom_1 (
    .addr(ROM_INPUT), .data({rom_1_data, WBSel, MemWEn, ALUSel, BSel, ASel, BrUn, ImmSel, RegWEn}));
  Comparator #(.width(7)) comparator_8 (.a(Instruction[31:25]), .b({7{1'b0}}), .eq(comparator_8_eq));  // open: gt, lt
  Comparator #(.width(7)) comparator_9 (.a(Instruction[31:25]), .b(7'b0000001), .eq(comparator_9_eq));  // open: gt, lt
  Comparator #(.width(7)) comparator_10 (
    .a(Instruction[31:25]), .b(7'b0100000), .eq(comparator_10_eq));  // open: gt, lt
  Comparator #(.width(7)) comparator_11 (.a(Instruction[31:25]), .b({7{1'b0}}), .eq(comparator_11_eq));  // open: gt, lt
  Comparator #(.width(7)) comparator_12 (
    .a(Instruction[31:25]), .b(7'b0000001), .eq(comparator_12_eq));  // open: gt, lt
  Comparator #(.width(7)) comparator_13 (.a(Instruction[31:25]), .b({7{1'b0}}), .eq(comparator_13_eq));  // open: gt, lt
  Comparator #(.width(7)) comparator_14 (
    .a(Instruction[31:25]), .b(7'b0100000), .eq(comparator_14_eq));  // open: gt, lt
  Comparator #(.width(3)) comparator_15 (.a(Instruction[14:12]), .b(3'b000), .eq(comparator_15_eq));  // open: gt, lt
  Comparator #(.width(3)) comparator_16 (.a(Instruction[14:12]), .b(3'b001), .eq(comparator_16_eq));  // open: gt, lt
  Comparator #(.width(3)) comparator_17 (.a(Instruction[14:12]), .b(3'b010), .eq(comparator_17_eq));  // open: gt, lt
  Comparator #(.width(3)) comparator_18 (.a(Instruction[14:12]), .b(3'b100), .eq(comparator_18_eq));  // open: gt, lt
  Comparator #(.width(3)) comparator_19 (.a(Instruction[14:12]), .b(3'b110), .eq(comparator_19_eq));  // open: gt, lt
  Comparator #(.width(3)) comparator_20 (.a(Instruction[14:12]), .b(3'b111), .eq(comparator_20_eq));  // open: gt, lt
  Comparator #(.width(3)) comparator_21 (.a(Instruction[14:12]), .b(3'b101), .eq(comparator_21_eq));  // open: gt, lt
  Comparator #(.width(3)) comparator_22 (.a(Instruction[14:12]), .b(3'b101), .eq(comparator_22_eq));  // open: gt, lt
  and and_1 (IS_SRAI, comparator_22_eq, IS_ARITH, IS_I);
  and and_2 (IS_ADD, IS_ADD_MUL_SUB, comparator_8_eq, IS_R);
  and and_3 (IS_MUL, IS_ADD_MUL_SUB, comparator_9_eq, IS_R);
  and and_4 (IS_SUB, IS_ADD_MUL_SUB, comparator_10_eq, IS_R);
  and and_5 (IS_SLL, IS_SLL_MULH, comparator_11_eq, IS_R);
  and and_6 (IS_MULH, IS_SLL_MULH, comparator_12_eq, IS_R);
  Comparator #(.width(3)) comparator_23 (.a(Instruction[14:12]), .b(3'b011), .eq(comparator_23_eq));  // open: gt, lt
  and and_7 (IS_MULHU, comparator_23_eq, IS_R);
  Comparator #(.width(3)) comparator_24 (.a(Instruction[14:12]), .b(3'b010), .eq(comparator_24_eq));  // open: gt, lt
  and and_8 (IS_SLT, comparator_24_eq, IS_R);
  Comparator #(.width(3)) comparator_25 (.a(Instruction[14:12]), .b(3'b100), .eq(comparator_25_eq));  // open: gt, lt
  and and_9 (IS_XOR, comparator_25_eq, IS_R);
  Comparator #(.width(3)) comparator_26 (.a(Instruction[14:12]), .b(3'b110), .eq(comparator_26_eq));  // open: gt, lt
  Comparator #(.width(3)) comparator_27 (.a(Instruction[14:12]), .b(3'b111), .eq(comparator_27_eq));  // open: gt, lt
  and and_10 (IS_ADDI, comparator_15_eq, IS_I);
  and and_11 (IS_SLLI, comparator_16_eq, IS_I);
  and and_12 (IS_SLTI, comparator_17_eq, IS_I);
  and and_13 (IS_XORI, comparator_18_eq, IS_I);
  and and_14 (IS_ORI, comparator_19_eq, IS_I);
  and and_15 (IS_ANDI, comparator_20_eq, IS_I);
  and and_16 (IS_SRLI, comparator_21_eq, IS_LOGICAL, IS_I);
  and and_17 (IS_SRL, IS_SRA_SRL, comparator_13_eq, IS_R);
  and and_18 (IS_SRA, IS_SRA_SRL, comparator_14_eq, IS_R);
  and and_19 (IS_OR, comparator_26_eq, IS_R);
  and and_20 (IS_AND, comparator_27_eq, IS_R);
  Priority_Encoder #(.select_enc(6)) priority_encoder_1 (
    .in0(IS_ADD), .in1(IS_MUL), .in2(IS_SUB), .in3(IS_SLL), .in4(IS_MULH), .in5(IS_MULHU), .in6(IS_SLT),
    .in7(IS_XOR), .in8(IS_SRL), .in9(IS_SRA), .in10(IS_OR), .in11(IS_AND), .in15(IS_ADDI), .in16(IS_SLLI),
    .in17(IS_SLTI), .in18(IS_XORI), .in19(IS_SRLI), .in20(IS_SRAI), .in21(IS_ORI), .in22(IS_ANDI),
    .out(ROM_INPUT));  // open: in12, in13, in14, in23, in24, in25, in26, in27, in28, in29, in30, in31, in32, in33, in34, in35, in36, in37, in38, in39, in40, in41, in42, in43, in44, in45, in46, in47, in48, in49, in50, in51, in52, in53, in54, in55, in56, in57, in58, in59, in60, in61, in62, in63, gs, en_out, en_in

  assign PCSel = 1'b0;

  // Other names for the same wires on the sheet: OPCODE[6:0] = Instruction[6:0]; FUNC3[2:0] = Instruction[14:12];
  //   FUNC7[6:0] = Instruction[31:25]

  // Notes on the sheet:
  //   INPUTS to your circuit
  //   Connect ROM Input here ->
  //   contents of rom_1 (hex, n*v repeats v):
  //   100f 140f 160f 108f 148f 158f 110f 120f 128f 168f 130f 138f 0 0 0 1041 10c1 1141 1241 12c1 16c1 1341
  //   13c1
  //   ROM FOR CONTROL LOGIC
  //   DON'T CHANGE THE LOCATIONS OF THE INPUTS AND OUTPUTS!
  //   This is only if you choose to do the ROM option
  //   CONNECT
  //   WIRE
  //   TO
  //   USE
  //   ROM
  //   OUTPUT from your circuit
  //   Reminder: If using ROM, use combinational logic for PCSel
endmodule
