// Logisim project cpu.circ as structural Verilog: 1 circuit, main circuit cpu
module cpu (
  input  clk,
  input  [31:0] Instruction,
  input  [31:0] MemReadData,
  output [31:0] MemAddress,
  output [31:0] ProgramCounter,
  output [31:0] ra,
  output [31:0] sp,
  output [31:0] t0,
  output [31:0] t1,
  output [31:0] t2,
  output [31:0] s0,
  output [31:0] s1,
  output [31:0] a0,
  output [3:0] MemWriteMask,
  output [31:0] MemWriteData
);

  wire ASEL, BREQ, BRLT, BRUN, BSEL, MEMWEN, PCSEL, REGWEN;
  wire [1:0] WBSEL;
  wire [2:0] IMMSEL;
  wire [3:0] ALUSEL;
  wire [31:0] adder_1_out, IMM, MEMout, multiplexer_1_out, multiplexer_2_out, multiplexer_3_out,
       multiplexer_4_out, READ1, READ2;

  Adder #(.width(32)) adder_1 (.a(ProgramCounter), .b(32'h4), .out(adder_1_out));  // open: cin, cout
  Register #(.width(32)) PC (.D(multiplexer_1_out), .clk(clk), .Q(ProgramCounter));  // open: en, clr
  Multiplexer #(.width(32)) multiplexer_1 (.in0(adder_1_out), .in1(MemAddress), .out(multiplexer_1_out), .sel(PCSEL));
  Multiplexer #(.select(2), .width(32)) multiplexer_2 (
    .in0(MEMout), .in1(MemAddress), .in2(adder_1_out), .out(multiplexer_2_out), .sel(WBSEL));  // open: in3
  control_logic control_logic_1 (
    .PCSel(PCSEL), .RegWEn(REGWEN), .ImmSel(IMMSEL), .BrUn(BRUN), .ASel(ASEL), .BSel(BSEL), .ALUSel(ALUSEL),
    .MemWEn(MEMWEN), .WBSel(WBSEL), .Instruction(Instruction), .BrEq(BREQ), .BrLt(BRLT));
  regfile regfile_1 (
    .ReadIndex1(Instruction[19:15]), .ReadIndex2(Instruction[24:20]), .WriteIndex(Instruction[11:7]),
    .WriteData(multiplexer_2_out), .RegWEn(REGWEN), .clk(clk), .ra(ra), .sp(sp), .t0(t0), .t1(t1), .t2(t2),
    .s0(s0), .s1(s1), .a0(a0), .ReadData1(READ1), .ReadData2(READ2));
  imm_gen imm_gen_1 (.Instruction(Instruction), .ImmSel(IMMSEL), .Immediate(IMM));
  Multiplexer #(.width(32)) multiplexer_3 (.in0(READ1), .in1(ProgramCounter), .out(multiplexer_3_out), .sel(ASEL));
  Multiplexer #(.width(32)) multiplexer_4 (.in0(READ2), .in1(IMM), .out(multiplexer_4_out), .sel(BSEL));
  alu alu_1 (.ALUResult(MemAddress), .A(multiplexer_3_out), .B(multiplexer_4_out), .ALUSel(ALUSEL));
  branch_comp branch_comp_1 (.BrData1(READ1), .BrData2(READ2), .BrUn(BRUN), .BrEq(BREQ), .BrLt(BRLT));
  partial_store partial_store_1 (
    .Instruction(Instruction), .MemAddress(MemAddress), .DataFromReg(READ2), .MemWEn(MEMWEN),
    .MemWriteMask(MemWriteMask), .DataToMem(MemWriteData));
  partial_load partial_load_1 (
    .Instruction(Instruction), .MemAddress(MemAddress), .DataFromMem(MemReadData), .DataToReg(MEMout));

  // Other names for the same wires on the sheet: ALUout[31:0] = MemAddress; RD[4:0] = Instruction[11:7];
  //   RS1[4:0] = Instruction[19:15]; RS2[4:0] = Instruction[24:20]

  // Notes on the sheet:
  //   To IMEM
  //   IMEM (do **NOT** move this)
  //   From IMEM
  //   Inputs/Outputs for testing. Do **NOT** move these.
  //   It is OK to move the PC, RegFile, ALU, MEM, Branch Comp, Imm Gen, Partial Load, Partial Store and Control Logic to wherever is most convenient for you when constructing your CPU, and to delete this text
  //   To DMEM
  //   DMEM (do **NOT** move this)
  //   From DMEM
endmodule
